# Fritzing sketch GOS (saved by Fritzing 0.9.3b)
breadboards: 1

parts:
  Composant1 = Arduino Mega 2560 (Rev3)
  Composant2 = MicroSD Card Module

nets:
  5V: Composant1.5V, Composant2.VCC
  GND: Composant1.GND, Composant2.GND
  N1: Composant1.D50, Composant2.MISO
  N2: Composant1.D51, Composant2.MOSI
  N3: Composant1.D52, Composant2.SCK
  N4: Composant1.D53, Composant2.CS
